// Digital circuit 20bitfxdpointmult.dig as structural Verilog
module _20bitfxdpointmult (
  input  [19:0] inA,
  input  [19:0] inB,
  output [19:0] _20bitfxdpntMultOUT
);

  wire [39:0] fxedpntMult_mul;

  Mul #(.Bits(20)) fxedpntMult (
    .a(inA), .b(inB), .mul({fxedpntMult_mul[39:32], _20bitfxdpntMultOUT, fxedpntMult_mul[11:0]}));
endmodule
