// Digital circuit ZOOMBROT.dig as structural Verilog
module ZOOMBROT (
  input  in_1,
  input  in_2,
  input  clk,
  input  enable,
  output [4:0] grey
);

  wire downn, ell, exx, kay, leftt, N_out, nor_1_out, R_out, rightt, rs_ff_as_1_q,
       signedcomplex_1_grtrthanfour, signedcomplex_2_grtrthanfour, signedcomplex_3_grtrthanfour,
       signedcomplex_4_grtrthanfour, signedcomplex_5_grtrthanfour, signedcomplex_6_grtrthanfour,
       signedcomplex_7_grtrthanfour, signedcomplex_8_grtrthanfour, signedcomplex_9_grtrthanfour,
       signedcomplex_10_grtrthanfour, signedcomplex_11_grtrthanfour, signedcomplex_12_grtrthanfour,
       signedcomplex_13_grtrthanfour, signedcomplex_14_grtrthanfour, signedcomplex_15_grtrthanfour,
       signedcomplex_16_grtrthanfour, upp, zee, zoompanmap_1_framedrawn, zoomtodec_1_p3;
  wire [3:0] zoompangen_1_panfactor, zoompangen_1_panfactor_2, zoomtodec_1_p2, zoomtodec_1_p4,
       zoomtodec_1_p5, zoomtodec_1_p6, zoomtodec_1_p7;
  wire [4:0] multiplexer_1_out, multiplexer_2_out, multiplexer_3_out, multiplexer_4_out, multiplexer_5_out,
       multiplexer_6_out, multiplexer_7_out, multiplexer_8_out, multiplexer_9_out, multiplexer_10_out,
       multiplexer_11_out, multiplexer_12_out, multiplexer_13_out, multiplexer_14_out, multiplexer_15_out,
       multiplexer_16_out, multiplexer_17_out;
  wire [7:0] zoompanmap_1_ycoord;
  wire [7:7] not_1_out, zoompanmap_1_xcoord_2;
  wire [13:0] zoompanmap_1_xcoord;
  wire [15:0] signedcomplex_1_newimage, signedcomplex_1_newreals, signedcomplex_2_newimage,
       signedcomplex_2_newreals, signedcomplex_3_newimage, signedcomplex_3_newreals,
       signedcomplex_4_newimage, signedcomplex_4_newreals, signedcomplex_5_newimage,
       signedcomplex_5_newreals, signedcomplex_6_newimage, signedcomplex_6_newreals,
       signedcomplex_7_newimage, signedcomplex_7_newreals, signedcomplex_8_newimage,
       signedcomplex_8_newreals, signedcomplex_9_newimage, signedcomplex_9_newreals,
       signedcomplex_10_newimage, signedcomplex_10_newreals, signedcomplex_11_newimage,
       signedcomplex_11_newreals, signedcomplex_12_newimage, signedcomplex_12_newreals,
       signedcomplex_13_newimage, signedcomplex_13_newreals, signedcomplex_14_newimage,
       signedcomplex_14_newreals, signedcomplex_15_newimage, signedcomplex_15_newreals,
       zoompanmap_1_mapimage, zoompanmap_1_mapreal;
  wire [15:10] graphiccard_1_d;
  wire [19:0] zoompangen_1_image_bound, zoompangen_1_real_bound, zoompangen_1_scalefactor;

  Button R (.out(R_out));
  Button K (.out(kay));
  Button L (.out(ell));
  Button RIGHT (.out(rightt));
  Button LEFT (.out(leftt));
  Button UP (.out(upp));
  Button DOWN (.out(downn));
  Button X (.out(exx));
  Button Z (.out(zee));
  LED led_1 (.in(exx));
  LED led_2 (.in(zee));
  zoompanGEN zoompangen_1 (
    .plus(kay), .in_2(ell), .left(leftt), .up(upp), .right(rightt), .down(downn), .clk(clk), .clr(R_out),
    .enable(enable), .scalefactor(zoompangen_1_scalefactor), .image_bound(zoompangen_1_image_bound),
    .real_bound(zoompangen_1_real_bound), .frame_drawn(clk), .morePAN(exx), .lessPAN(zee),
    .panfactor({zoompangen_1_panfactor_2, zoompangen_1_panfactor}));
  Button N (.out(N_out));
  Seven_Seg_Hex seven_seg_hex_1 (.d(zoompangen_1_panfactor_2), .dp(1'b0));
  Seven_Seg_Hex seven_seg_hex_2 (.d(zoompangen_1_panfactor), .dp(1'b0));
  RS_FF_AS rs_ff_as_1 (.S(zoompanmap_1_framedrawn), .R(N_out), .Q(rs_ff_as_1_q));  // open: nQ
  zoompanMAP zoompanmap_1 (
    .mapREAL(zoompanmap_1_mapreal), .Xcoord({zoompanmap_1_xcoord_2[7], zoompanmap_1_xcoord[6:0]}),
    .enable(enable), .real_bound(zoompangen_1_real_bound), .imaginary_bound(zoompangen_1_image_bound),
    .scale_factor(zoompangen_1_scalefactor), .clr(N_out), .Ycoord(zoompanmap_1_ycoord),
    .mapIMAGE(zoompanmap_1_mapimage), .clk(clk), .framedrawn(zoompanmap_1_framedrawn));
  LED FRAME_DRAWN (.in(rs_ff_as_1_q));
  LED led_3 (.in(leftt));
  // zoomtoDec zoomtodec_1: pin names not known; wires that end beside it: zoompangen_1_scalefactor, zoomtodec_1_p2, zoomtodec_1_p3, zoomtodec_1_p4, zoomtodec_1_p5, zoomtodec_1_p6, zoomtodec_1_p7
  assign {not_1_out[7], zoompanmap_1_xcoord[13:7]} = ~zoompanmap_1_ycoord;  // Not not_1, 8 bits wide
  LED led_4 (.in(upp));
  LED led_5 (.in(downn));
  LED led_6 (.in(rightt));
  signedCOMPLEX signedcomplex_1 (
    .newIMAGE(signedcomplex_1_newimage), .A(zoompanmap_1_mapreal), .B(zoompanmap_1_mapimage),
    .newREALS(signedcomplex_1_newreals), .grtrThanFOUR(signedcomplex_1_grtrthanfour),
    .A_0(zoompanmap_1_mapreal), .B_0(zoompanmap_1_mapimage));
  LED led_7 (.in(ell));
  LED led_8 (.in(kay));
  GraphicCard #(.graphicHeight(128), .graphicWidth(128), .Bits(16)) graphiccard_1 (
    .A({1'b0, zoompanmap_1_xcoord}), .str(enable), .C(clk), .ld(in_1), .B(in_2),
    .D({graphiccard_1_d, grey, grey}));
  signedCOMPLEX signedcomplex_2 (
    .newIMAGE(signedcomplex_2_newimage), .A(signedcomplex_1_newreals), .B(signedcomplex_1_newimage),
    .newREALS(signedcomplex_2_newreals), .grtrThanFOUR(signedcomplex_2_grtrthanfour),
    .A_0(zoompanmap_1_mapreal), .B_0(zoompanmap_1_mapimage));
  Multiplexer #(.Bits(5)) multiplexer_1 (
    .sel(signedcomplex_1_grtrthanfour), .in_0({5{1'b0}}), .in_1({5{1'b1}}), .out(multiplexer_1_out));
  Seven_Seg_Hex seven_seg_hex_3 (.d(zoomtodec_1_p7), .dp(1'b0));
  signedCOMPLEX signedcomplex_3 (
    .newIMAGE(signedcomplex_3_newimage), .A(signedcomplex_2_newreals), .B(signedcomplex_2_newimage),
    .newREALS(signedcomplex_3_newreals), .grtrThanFOUR(signedcomplex_3_grtrthanfour),
    .A_0(zoompanmap_1_mapreal), .B_0(zoompanmap_1_mapimage));
  Multiplexer #(.Bits(5)) multiplexer_2 (
    .sel(signedcomplex_2_grtrthanfour), .in_0({5{1'b0}}), .in_1(5'b11101), .out(multiplexer_2_out));
  Seven_Seg_Hex seven_seg_hex_4 (.d(zoomtodec_1_p6), .dp(1'b0));
  signedCOMPLEX signedcomplex_4 (
    .newIMAGE(signedcomplex_4_newimage), .A(signedcomplex_3_newreals), .B(signedcomplex_3_newimage),
    .newREALS(signedcomplex_4_newreals), .grtrThanFOUR(signedcomplex_4_grtrthanfour),
    .A_0(zoompanmap_1_mapreal), .B_0(zoompanmap_1_mapimage));
  Multiplexer #(.Bits(5)) multiplexer_3 (
    .sel(signedcomplex_3_grtrthanfour), .in_0({5{1'b0}}), .in_1(5'b11011), .out(multiplexer_3_out));
  Seven_Seg_Hex seven_seg_hex_5 (.d(zoomtodec_1_p5), .dp(1'b0));
  signedCOMPLEX signedcomplex_5 (
    .newIMAGE(signedcomplex_5_newimage), .A(signedcomplex_4_newreals), .B(signedcomplex_4_newimage),
    .newREALS(signedcomplex_5_newreals), .grtrThanFOUR(signedcomplex_5_grtrthanfour),
    .A_0(zoompanmap_1_mapreal), .B_0(zoompanmap_1_mapimage));
  Multiplexer #(.Bits(5)) multiplexer_4 (
    .sel(signedcomplex_4_grtrthanfour), .in_0({5{1'b0}}), .in_1(5'b11001), .out(multiplexer_4_out));
  Seven_Seg_Hex seven_seg_hex_6 (.d(zoomtodec_1_p4), .dp(1'b0));
  Seven_Seg seven_seg_1 (.a(1'b0), .b(1'b0), .c(1'b0), .d(1'b0), .e(1'b0), .f(1'b0), .g(zoomtodec_1_p3), .dp(1'b0));
  signedCOMPLEX signedcomplex_6 (
    .newIMAGE(signedcomplex_6_newimage), .A(signedcomplex_5_newreals), .B(signedcomplex_5_newimage),
    .newREALS(signedcomplex_6_newreals), .grtrThanFOUR(signedcomplex_6_grtrthanfour),
    .A_0(zoompanmap_1_mapreal), .B_0(zoompanmap_1_mapimage));
  Multiplexer #(.Bits(5)) multiplexer_5 (
    .sel(signedcomplex_5_grtrthanfour), .in_0({5{1'b0}}), .in_1(5'b10111), .out(multiplexer_5_out));
  Seven_Seg_Hex seven_seg_hex_7 (.d(zoomtodec_1_p2), .dp(1'b0));
  signedCOMPLEX signedcomplex_7 (
    .newIMAGE(signedcomplex_7_newimage), .A(signedcomplex_6_newreals), .B(signedcomplex_6_newimage),
    .newREALS(signedcomplex_7_newreals), .grtrThanFOUR(signedcomplex_7_grtrthanfour),
    .A_0(zoompanmap_1_mapreal), .B_0(zoompanmap_1_mapimage));
  Multiplexer #(.Bits(5)) multiplexer_6 (
    .sel(signedcomplex_6_grtrthanfour), .in_0({5{1'b0}}), .in_1(5'b10101), .out(multiplexer_6_out));
  nor nor_1 (nor_1_out, signedcomplex_1_grtrthanfour, signedcomplex_2_grtrthanfour, signedcomplex_3_grtrthanfour, signedcomplex_4_grtrthanfour, signedcomplex_5_grtrthanfour, signedcomplex_6_grtrthanfour, signedcomplex_7_grtrthanfour, signedcomplex_8_grtrthanfour, signedcomplex_9_grtrthanfour, signedcomplex_10_grtrthanfour, signedcomplex_11_grtrthanfour, signedcomplex_12_grtrthanfour, signedcomplex_13_grtrthanfour, signedcomplex_14_grtrthanfour, signedcomplex_15_grtrthanfour, signedcomplex_16_grtrthanfour);
  signedCOMPLEX signedcomplex_8 (
    .newIMAGE(signedcomplex_8_newimage), .A(signedcomplex_7_newreals), .B(signedcomplex_7_newimage),
    .newREALS(signedcomplex_8_newreals), .grtrThanFOUR(signedcomplex_8_grtrthanfour),
    .A_0(zoompanmap_1_mapreal), .B_0(zoompanmap_1_mapimage));
  Multiplexer #(.Bits(5)) multiplexer_7 (
    .sel(signedcomplex_7_grtrthanfour), .in_0({5{1'b0}}), .in_1(5'b10011), .out(multiplexer_7_out));
  signedCOMPLEX signedcomplex_9 (
    .newIMAGE(signedcomplex_9_newimage), .A(signedcomplex_8_newreals), .B(signedcomplex_8_newimage),
    .newREALS(signedcomplex_9_newreals), .grtrThanFOUR(signedcomplex_9_grtrthanfour),
    .A_0(zoompanmap_1_mapreal), .B_0(zoompanmap_1_mapimage));
  Multiplexer #(.Bits(5)) multiplexer_8 (
    .sel(signedcomplex_8_grtrthanfour), .in_0({5{1'b0}}), .in_1(5'b10001), .out(multiplexer_8_out));
  signedCOMPLEX signedcomplex_10 (
    .newIMAGE(signedcomplex_10_newimage), .A(signedcomplex_9_newreals), .B(signedcomplex_9_newimage),
    .newREALS(signedcomplex_10_newreals), .grtrThanFOUR(signedcomplex_10_grtrthanfour),
    .A_0(zoompanmap_1_mapreal), .B_0(zoompanmap_1_mapimage));
  Multiplexer #(.Bits(5)) multiplexer_9 (
    .sel(signedcomplex_9_grtrthanfour), .in_0({5{1'b0}}), .in_1(5'b01111), .out(multiplexer_9_out));
  signedCOMPLEX signedcomplex_11 (
    .newIMAGE(signedcomplex_11_newimage), .A(signedcomplex_10_newreals), .B(signedcomplex_10_newimage),
    .newREALS(signedcomplex_11_newreals), .grtrThanFOUR(signedcomplex_11_grtrthanfour),
    .A_0(zoompanmap_1_mapreal), .B_0(zoompanmap_1_mapimage));
  Multiplexer #(.Bits(5)) multiplexer_10 (
    .sel(signedcomplex_10_grtrthanfour), .in_0({5{1'b0}}), .in_1(5'b01101), .out(multiplexer_10_out));
  assign grey = multiplexer_17_out | multiplexer_16_out | multiplexer_15_out | multiplexer_14_out | multiplexer_13_out | multiplexer_12_out | multiplexer_11_out | multiplexer_10_out | multiplexer_9_out | multiplexer_8_out | multiplexer_7_out | multiplexer_6_out | multiplexer_5_out | multiplexer_4_out | multiplexer_3_out | multiplexer_2_out | multiplexer_1_out;  // Or or_1, 5 bits wide
  signedCOMPLEX signedcomplex_12 (
    .newIMAGE(signedcomplex_12_newimage), .A(signedcomplex_11_newreals), .B(signedcomplex_11_newimage),
    .newREALS(signedcomplex_12_newreals), .grtrThanFOUR(signedcomplex_12_grtrthanfour),
    .A_0(zoompanmap_1_mapreal), .B_0(zoompanmap_1_mapimage));
  Multiplexer #(.Bits(5)) multiplexer_11 (
    .sel(signedcomplex_11_grtrthanfour), .in_0({5{1'b0}}), .in_1(5'b01011), .out(multiplexer_11_out));
  signedCOMPLEX signedcomplex_13 (
    .newIMAGE(signedcomplex_13_newimage), .A(signedcomplex_12_newreals), .B(signedcomplex_12_newimage),
    .newREALS(signedcomplex_13_newreals), .grtrThanFOUR(signedcomplex_13_grtrthanfour),
    .A_0(zoompanmap_1_mapreal), .B_0(zoompanmap_1_mapimage));
  Multiplexer #(.Bits(5)) multiplexer_12 (
    .sel(signedcomplex_12_grtrthanfour), .in_0({5{1'b0}}), .in_1(5'b01001), .out(multiplexer_12_out));
  signedCOMPLEX signedcomplex_14 (
    .newIMAGE(signedcomplex_14_newimage), .A(signedcomplex_13_newreals), .B(signedcomplex_13_newimage),
    .newREALS(signedcomplex_14_newreals), .grtrThanFOUR(signedcomplex_14_grtrthanfour),
    .A_0(zoompanmap_1_mapreal), .B_0(zoompanmap_1_mapimage));
  Multiplexer #(.Bits(5)) multiplexer_13 (
    .sel(signedcomplex_13_grtrthanfour), .in_0({5{1'b0}}), .in_1(5'b00111), .out(multiplexer_13_out));
  signedCOMPLEX signedcomplex_15 (
    .newIMAGE(signedcomplex_15_newimage), .A(signedcomplex_14_newreals), .B(signedcomplex_14_newimage),
    .newREALS(signedcomplex_15_newreals), .grtrThanFOUR(signedcomplex_15_grtrthanfour),
    .A_0(zoompanmap_1_mapreal), .B_0(zoompanmap_1_mapimage));
  Multiplexer #(.Bits(5)) multiplexer_14 (
    .sel(signedcomplex_14_grtrthanfour), .in_0({5{1'b0}}), .in_1(5'b00101), .out(multiplexer_14_out));
  signedCOMPLEX signedcomplex_16 (
    .A(signedcomplex_15_newreals), .B(signedcomplex_15_newimage),
    .grtrThanFOUR(signedcomplex_16_grtrthanfour), .A_0(zoompanmap_1_mapreal), .B_0(zoompanmap_1_mapimage));  // open: newIMAGE, newREALS
  Multiplexer #(.Bits(5)) multiplexer_15 (
    .sel(signedcomplex_15_grtrthanfour), .in_0({5{1'b0}}), .in_1(5'b00011), .out(multiplexer_15_out));
  Multiplexer #(.Bits(5)) multiplexer_16 (
    .sel(signedcomplex_16_grtrthanfour), .in_0({5{1'b0}}), .in_1(5'b00001), .out(multiplexer_16_out));
  Multiplexer #(.Bits(5)) multiplexer_17 (
    .sel(nor_1_out), .in_0({5{1'b0}}), .in_1({5{1'b0}}), .out(multiplexer_17_out));
  // also tied to GND on the sheet: {graphiccard_1_d[10], graphiccard_1_d[11], graphiccard_1_d[12], graphiccard_1_d[13], graphiccard_1_d[14]}
  // also tied to VCC on the sheet: graphiccard_1_d[15]

  // Notes on the sheet:
  //   clk: Hz: 5000
  //   Pixels Per Pan
  //   PAN:............................< ^ > v
  //   +PanAmount:..................X
  //   -PanAmount:...................Z
  //   +Zoom :............................L
  //   -Zoom:..............................K
  //   Draw Frame....................N
  //   TOGGLE CLOCK..........SPCE
  //   RESET TO DEFAULT:...R
  //   ZOOM LEVEL
endmodule
