// Digital circuit absunit.dig as structural Verilog
module absunit (
  input  [15:0] absin,
  output [15:0] absout
);

  wire pulldown_1_out;
  wire [15:0] add_1_s, not_1_out;

  assign not_1_out = ~absin;  // Not not_1, 16 bits wide
  Add #(.Bits(16)) add_1 (.a(not_1_out), .b(16'h1), .c_i(pulldown_1_out), .s(add_1_s));  // open: c_o
  PullDown pulldown_1 (.out(pulldown_1_out));
  Multiplexer #(.Bits(16)) multiplexer_1 (.sel(absin[15]), .in_0(absin), .in_1(add_1_s), .out(absout));
endmodule
