// Digital circuit fixedpointmult.dig as structural Verilog
module fixedpointmult (
  input  [15:0] inA,
  input  [15:0] inB,
  output [15:0] fxdpntMultOUT
);

  wire [31:0] fxedpntMult_mul;

  Mul #(.Bits(16)) fxedpntMult (.a(inA), .b(inB), .mul({fxedpntMult_mul[31:28], fxdpntMultOUT, fxedpntMult_mul[11:0]}));
endmodule
