// Digital circuit signedCOMPLEX.dig as structural Verilog
module signedCOMPLEX (
  input  [15:0] A,
  input  [15:0] B,
  input  [15:0] A_0,
  input  [15:0] B_0,
  output [15:0] newIMAGE,
  output [15:0] newREALS,
  output grtrThanFOUR
);

  wire pulldown_1_out, pulldown_2_out, pulldown_3_out, xor_1_out;
  wire [15:0] absunit_1_absout, absunit_2_absout, absunit_3_absout, absunit_4_absout, absunit_5_absout,
       absunit_6_absout, add_1_s, add_2_s, add_3_s, arithmetic_shift_out, fixedpointmult_1_fxdpntmultout,
       fixedpointmult_2_fxdpntmultout, fixedpointmult_3_fxdpntmultout, fixedpointmult_4_fxdpntmultout,
       fixedpointmult_5_fxdpntmultout, multiplexer_1_out, neg_1_out, sub_1_s;

  absunit absunit_1 (.absin(A), .absout(absunit_1_absout));
  absunit absunit_2 (.absin(B), .absout(absunit_2_absout));
  fixedpointmult fixedpointmult_1 (
    .inA(absunit_1_absout), .inB(absunit_1_absout), .fxdpntMultOUT(fixedpointmult_1_fxdpntmultout));
  fixedpointmult fixedpointmult_2 (
    .inA(absunit_2_absout), .inB(absunit_2_absout), .fxdpntMultOUT(fixedpointmult_2_fxdpntmultout));
  PullDown pulldown_1 (.out(pulldown_1_out));
  absunit absunit_3 (.absin(B), .absout(absunit_3_absout));
  Sub #(.Bits(16)) sub_1 (
    .a(fixedpointmult_1_fxdpntmultout), .b(fixedpointmult_2_fxdpntmultout), .c_i(pulldown_1_out), .s(sub_1_s));  // open: c_o
  Add #(.Bits(16)) add_1 (.a(A_0), .b(sub_1_s), .c_i(pulldown_1_out), .s(add_1_s));  // open: c_o
  absunit absunit_4 (.absin(A), .absout(absunit_4_absout));
  absunit absunit_5 (.absin(add_1_s), .absout(absunit_5_absout));
  absunit absunit_6 (.absin(multiplexer_1_out), .absout(absunit_6_absout));
  fixedpointmult fixedpointmult_3 (
    .inA(absunit_4_absout), .inB(absunit_3_absout), .fxdpntMultOUT(fixedpointmult_3_fxdpntmultout));
  BarrelShifter #(.barrelShifterMode("arithmetic"), .Bits(16)) arithmetic_shift (
    .in(fixedpointmult_3_fxdpntmultout), .shift(5'b00001), .out(arithmetic_shift_out));
  fixedpointmult fixedpointmult_4 (
    .inA(absunit_5_absout), .inB(absunit_5_absout), .fxdpntMultOUT(fixedpointmult_4_fxdpntmultout));
  fixedpointmult fixedpointmult_5 (
    .inA(absunit_6_absout), .inB(absunit_6_absout), .fxdpntMultOUT(fixedpointmult_5_fxdpntmultout));
  Neg #(.Bits(16)) neg_1 (.in(arithmetic_shift_out), .out(neg_1_out));
  xor xor_1 (xor_1_out, A[15], B[15]);
  Multiplexer #(.Bits(16)) multiplexer_1 (
    .sel(xor_1_out), .in_0(arithmetic_shift_out), .in_1(neg_1_out), .out(multiplexer_1_out));
  Add #(.Bits(16)) add_2 (
    .a(fixedpointmult_4_fxdpntmultout), .b(fixedpointmult_5_fxdpntmultout), .c_i(pulldown_2_out), .s(add_2_s));  // open: c_o
  PullDown pulldown_2 (.out(pulldown_2_out));
  PullDown pulldown_3 (.out(pulldown_3_out));
  Add #(.Bits(16)) add_3 (.a(B_0), .b(multiplexer_1_out), .c_i(pulldown_3_out), .s(add_3_s));  // open: c_o
  Comparator #(.Bits(16)) comparator_1 (.a(add_2_s), .b(16'h4000), .gt(grtrThanFOUR));  // open: eq, lt
  Multiplexer #(.Bits(16)) multiplexer_2 (.sel(grtrThanFOUR), .in_0(add_1_s), .in_1({16{1'b0}}), .out(newREALS));
  Multiplexer #(.Bits(16)) multiplexer_3 (.sel(grtrThanFOUR), .in_0(add_3_s), .in_1({16{1'b0}}), .out(newIMAGE));

  // Notes on the sheet:
  //   a
  //   a^2
  //   b^2
  //   real = a^2 - b^2 + a_0
  //   2*a*b
  //   2*a*b + b_0
endmodule
