// Digital circuit zoompanGEN.dig as structural Verilog
module zoompanGEN (
  input  plus,
  input  in_2,
  input  left,
  input  up,
  input  right,
  input  down,
  input  clk,
  input  clr,
  input  enable,
  input  frame_drawn,
  input  morePAN,
  input  lessPAN,
  output [19:0] scalefactor,
  output [19:0] image_bound,
  output [19:0] real_bound,
  output [7:0] panfactor
);

  wire and_1_out, and_2_out, and_3_out, and_4_out, and_5_out, and_6_out, and_7_out, and_8_out,
       comparator_1_eq, comparator_2_eq, comparator_3_eq, comparator_4_eq, counter_1_ovf, or_1_out, or_2_out,
       or_3_out, or_4_out, or_5_out, or_8_out;
  wire [7:0] barrelshifter_3_out, barrelshifter_4_out, multiplexer_1_out, multiplexer_7_out,
       multiplexer_13_out, multiplexer_14_out, or_10_out, register_4_q;
  wire [9:0] counter_1_out;
  wire [19:0] _20bitfxdpointmult_1__20bitfxdpntmultout, add_1_s, add_2_s, add_3_s, add_4_s,
       barrelshifter_1_out, barrelshifter_2_out, multiplexer_2_out, multiplexer_3_out, multiplexer_4_out,
       multiplexer_5_out, multiplexer_6_out, multiplexer_8_out, multiplexer_9_out, multiplexer_10_out,
       multiplexer_11_out, multiplexer_12_out, not_1_out, not_2_out, or_6_out, or_7_out, or_9_out,
       register_1_q, register_2_q, register_3_q;

  Counter #(.Bits(10)) counter_1 (.en(enable), .C(clk), .clr(1'b0), .out(counter_1_out), .ovf(counter_1_ovf));
  Multiplexer #(.Bits(8)) multiplexer_1 (.sel(clr), .in_0(or_10_out), .in_1(8'h1), .out(multiplexer_1_out));
  Multiplexer #(.Bits(20)) multiplexer_2 (.sel(clr), .in_0(or_9_out), .in_1(20'h80), .out(multiplexer_2_out));
  Multiplexer #(.Bits(20)) multiplexer_3 (.sel(clr), .in_0(or_6_out), .in_1(20'hfe000), .out(multiplexer_3_out));
  Multiplexer #(.Bits(20)) multiplexer_4 (.sel(clr), .in_0(or_7_out), .in_1(20'hfe000), .out(multiplexer_4_out));
  Comparator #(.Bits(20)) comparator_1 (.a(register_1_q), .b(20'h1), .eq(comparator_1_eq));  // open: gt, lt
  Register #(.Bits(20)) register_1 (.D(multiplexer_2_out), .C(counter_1_ovf), .en(or_1_out), .Q(register_1_q));
  Register #(.Bits(20)) register_2 (.D(multiplexer_3_out), .C(counter_1_ovf), .en(or_3_out), .Q(register_2_q));
  Register #(.Bits(20)) register_3 (.D(multiplexer_4_out), .C(counter_1_ovf), .en(or_4_out), .Q(register_3_q));
  Comparator #(.Bits(8)) comparator_2 (.a(register_4_q), .b(8'h1), .eq(comparator_2_eq));  // open: gt, lt
  and and_1 (and_1_out, ~in_2, comparator_3_eq);  // And
  and and_2 (and_2_out, ~plus, comparator_1_eq);  // And
  Comparator #(.Bits(20)) comparator_3 (.a(register_1_q), .b(20'h80000), .eq(comparator_3_eq));  // open: gt, lt
  and and_3 (and_3_out, ~lessPAN, comparator_4_eq);  // And
  Comparator #(.Bits(8)) comparator_4 (.a(register_4_q), .b(8'h80), .eq(comparator_4_eq));  // open: gt, lt
  Register #(.Bits(8)) register_4 (.D(multiplexer_1_out), .C(counter_1_ovf), .en(or_2_out), .Q(register_4_q));
  Add #(.Bits(20)) add_1 (
    .a(register_2_q), .b(_20bitfxdpointmult_1__20bitfxdpntmultout), .c_i(1'b0), .s(add_1_s));  // open: c_o
  assign not_1_out = ~_20bitfxdpointmult_1__20bitfxdpntmultout;  // Not not_1, 20 bits wide
  Add #(.Bits(20)) add_2 (
    .a(register_3_q), .b(_20bitfxdpointmult_1__20bitfxdpntmultout), .c_i(1'b0), .s(add_2_s));  // open: c_o
  assign not_2_out = ~_20bitfxdpointmult_1__20bitfxdpntmultout;  // Not not_2, 20 bits wide
  Add #(.Bits(20)) add_3 (.a(register_3_q), .b(not_2_out), .c_i(1'b1), .s(add_3_s));  // open: c_o
  _20bitfxdpointmult _20bitfxdpointmult_1 (
    .inA(register_1_q), .inB({register_4_q, {12{1'b0}}}),
    ._20bitfxdpntMultOUT(_20bitfxdpointmult_1__20bitfxdpntmultout));
  and and_4 (and_4_out, ~morePAN, comparator_2_eq);  // And
  or or_1 (or_1_out, in_2, clr, plus);
  and and_5 (and_5_out, ~and_2_out, in_2);  // And
  Multiplexer #(.Bits(20)) multiplexer_5 (
    .sel(and_5_out), .in_0({20{1'b0}}), .in_1(register_1_q), .out(multiplexer_5_out));
  Multiplexer #(.Bits(20)) multiplexer_6 (
    .sel(and_7_out), .in_0({20{1'b0}}), .in_1(register_1_q), .out(multiplexer_6_out));
  Add #(.Bits(20)) add_4 (.a(register_2_q), .b(not_1_out), .c_i(1'b1), .s(add_4_s));  // open: c_o
  or or_2 (or_2_out, lessPAN, clr, morePAN);
  and and_6 (and_6_out, ~and_4_out, lessPAN);  // And
  Multiplexer #(.Bits(8)) multiplexer_7 (
    .sel(and_6_out), .in_0({8{1'b0}}), .in_1(register_4_q), .out(multiplexer_7_out));
  and and_7 (and_7_out, plus, ~and_1_out);  // And
  Multiplexer #(.Bits(20)) multiplexer_8 (
    .sel(or_5_out), .in_0({20{1'b0}}), .in_1(register_1_q), .out(multiplexer_8_out));
  or or_3 (or_3_out, up, clr, down);
  Multiplexer #(.Bits(20)) multiplexer_9 (.sel(up), .in_0({20{1'b0}}), .in_1(add_1_s), .out(multiplexer_9_out));
  Multiplexer #(.Bits(20)) multiplexer_10 (.sel(down), .in_0({20{1'b0}}), .in_1(add_4_s), .out(multiplexer_10_out));
  or or_4 (or_4_out, right, clr, left);
  Multiplexer #(.Bits(20)) multiplexer_11 (.sel(right), .in_0({20{1'b0}}), .in_1(add_2_s), .out(multiplexer_11_out));
  Multiplexer #(.Bits(20)) multiplexer_12 (.sel(left), .in_0({20{1'b0}}), .in_1(add_3_s), .out(multiplexer_12_out));
  and and_8 (and_8_out, morePAN, ~and_3_out);  // And
  Multiplexer #(.Bits(8)) multiplexer_13 (
    .sel(and_8_out), .in_0({8{1'b0}}), .in_1(register_4_q), .out(multiplexer_13_out));
  Multiplexer #(.Bits(8)) multiplexer_14 (
    .sel(or_8_out), .in_0({8{1'b0}}), .in_1(register_4_q), .out(multiplexer_14_out));
  or or_5 (or_5_out, and_1_out, and_2_out);
  assign or_6_out = multiplexer_9_out | multiplexer_10_out;  // Or or_6, 20 bits wide
  assign or_7_out = multiplexer_11_out | multiplexer_12_out;  // Or or_7, 20 bits wide
  or or_8 (or_8_out, and_3_out, and_4_out);
  BarrelShifter #(.Bits(20), .direction("right")) barrelshifter_1 (
    .in(multiplexer_5_out), .shift(5'b00001), .out(barrelshifter_1_out));
  BarrelShifter #(.Bits(20)) barrelshifter_2 (.in(multiplexer_6_out), .shift(5'b00001), .out(barrelshifter_2_out));
  BarrelShifter #(.Bits(8), .direction("right")) barrelshifter_3 (
    .in(multiplexer_7_out), .shift(4'b0001), .out(barrelshifter_3_out));
  BarrelShifter #(.Bits(8)) barrelshifter_4 (.in(multiplexer_13_out), .shift(4'b0001), .out(barrelshifter_4_out));
  assign or_9_out = barrelshifter_1_out | multiplexer_8_out | barrelshifter_2_out;  // Or or_9, 20 bits wide
  assign or_10_out = barrelshifter_3_out | multiplexer_14_out | barrelshifter_4_out;  // Or or_10, 8 bits wide
  Register #(.Bits(20)) register_5 (.D(register_1_q), .C(clk), .en(frame_drawn), .Q(scalefactor));
  Register #(.Bits(20)) register_6 (.D(register_2_q), .C(clk), .en(frame_drawn), .Q(image_bound));
  Register #(.Bits(20)) register_7 (.D(register_3_q), .C(clk), .en(frame_drawn), .Q(real_bound));
  Register #(.Bits(8)) register_8 (.D(register_4_q), .C(clk), .en(frame_drawn), .Q(panfactor));
endmodule
