// Digital circuit zoompanMAP.dig as structural Verilog
module zoompanMAP (
  input  enable,
  input  [19:0] real_bound,
  input  [19:0] imaginary_bound,
  input  [19:0] scale_factor,
  input  clr,
  input  clk,
  output [15:0] mapREAL,
  output [7:0] Xcoord,
  output [7:0] Ycoord,
  output [15:0] mapIMAGE,
  output framedrawn
);

  wire and_1_out, counter_1_ovf, rs_ff_1_nq;
  wire [19:0] _20bitfxdpointmult_1__20bitfxdpntmultout, _20bitfxdpointmult_2__20bitfxdpntmultout;
  wire [19:16] add_1_s, add_2_s;

  RS_FF rs_ff_1 (.S(framedrawn), .C(clk), .R(clr), .nQ(rs_ff_1_nq));  // open: Q
  Counter #(.Bits(7)) counter_1 (.en(enable), .C(and_1_out), .clr(clr), .out(Xcoord[6:0]), .ovf(counter_1_ovf));
  Counter #(.Bits(7)) counter_2 (.en(counter_1_ovf), .C(and_1_out), .clr(clr), .out(Ycoord[6:0]), .ovf(framedrawn));
  and and_1 (and_1_out, rs_ff_1_nq, clk);
  _20bitfxdpointmult _20bitfxdpointmult_1 (
    .inA({1'b0, Xcoord[6:0], {12{1'b0}}}), .inB(scale_factor),
    ._20bitfxdpntMultOUT(_20bitfxdpointmult_1__20bitfxdpntmultout));
  _20bitfxdpointmult _20bitfxdpointmult_2 (
    .inA({1'b0, Ycoord[6:0], {12{1'b0}}}), .inB(scale_factor),
    ._20bitfxdpntMultOUT(_20bitfxdpointmult_2__20bitfxdpntmultout));
  Add #(.Bits(20)) add_1 (
    .a(_20bitfxdpointmult_1__20bitfxdpntmultout), .b(real_bound), .c_i(1'b0), .s({add_1_s, mapREAL}));  // open: c_o
  Add #(.Bits(20)) add_2 (
    .a(_20bitfxdpointmult_2__20bitfxdpntmultout), .b(imaginary_bound), .c_i(1'b0), .s({add_2_s, mapIMAGE}));  // open: c_o

  assign Xcoord[7] = 1'b0;
  assign Ycoord[7] = 1'b0;

  // Notes on the sheet:
  //   8.12 notation
endmodule
