// Digital circuit zoomtoDec.dig as structural Verilog
module zoomtoDec (
  input  [19:0] ZoomFactor,
  output [3:0] _0_1,
  output _1,
  output [3:0] _2,
  output [3:0] _3,
  output [3:0] _4,
  output [3:0] _5
);

  wire comparator_1_eq, comparator_2_eq, comparator_3_eq, comparator_4_eq, comparator_5_eq, comparator_6_eq,
       comparator_7_eq, comparator_8_eq, comparator_9_eq, comparator_10_eq, comparator_11_eq,
       comparator_12_eq, comparator_13_eq, comparator_14_eq, comparator_15_eq, comparator_16_eq,
       comparator_17_eq, comparator_18_eq, comparator_19_eq, comparator_20_eq, or_3_out, or_4_out, or_6_out,
       or_7_out, or_8_out, or_9_out, or_10_out, or_12_out, or_14_out;
  wire [3:0] multiplexer_1_out, multiplexer_2_out, multiplexer_3_out, multiplexer_4_out, multiplexer_5_out,
       multiplexer_6_out, multiplexer_7_out, multiplexer_8_out, multiplexer_9_out, multiplexer_10_out,
       multiplexer_11_out, multiplexer_12_out, multiplexer_13_out, multiplexer_14_out, multiplexer_16_out,
       multiplexer_17_out, multiplexer_18_out, multiplexer_19_out;

  Comparator #(.Bits(20)) comparator_1 (.a(ZoomFactor), .b(20'h1), .eq(comparator_1_eq));  // open: gt, lt
  Comparator #(.Bits(20)) comparator_2 (.a(ZoomFactor), .b(20'h2), .eq(comparator_2_eq));  // open: gt, lt
  Comparator #(.Bits(20)) comparator_3 (.a(ZoomFactor), .b(20'h4), .eq(comparator_3_eq));  // open: gt, lt
  Comparator #(.Bits(20)) comparator_4 (.a(ZoomFactor), .b(20'h8), .eq(comparator_4_eq));  // open: gt, lt
  Comparator #(.Bits(20)) comparator_5 (.a(ZoomFactor), .b(20'h10), .eq(comparator_5_eq));  // open: gt, lt
  Comparator #(.Bits(20)) comparator_6 (.a(ZoomFactor), .b(20'h20), .eq(comparator_6_eq));  // open: gt, lt
  Comparator #(.Bits(20)) comparator_7 (.a(ZoomFactor), .b(20'h40), .eq(comparator_7_eq));  // open: gt, lt
  Comparator #(.Bits(20)) comparator_8 (.a(ZoomFactor), .b(20'h80), .eq(comparator_8_eq));  // open: gt, lt
  Comparator #(.Bits(20)) comparator_9 (.a(ZoomFactor), .b(20'h100), .eq(comparator_9_eq));  // open: gt, lt
  Comparator #(.Bits(20)) comparator_10 (.a(ZoomFactor), .b(20'h200), .eq(comparator_10_eq));  // open: gt, lt
  Comparator #(.Bits(20)) comparator_11 (.a(ZoomFactor), .b(20'h400), .eq(comparator_11_eq));  // open: gt, lt
  Comparator #(.Bits(20)) comparator_12 (.a(ZoomFactor), .b(20'h800), .eq(comparator_12_eq));  // open: gt, lt
  Comparator #(.Bits(20)) comparator_13 (.a(ZoomFactor), .b(20'h1000), .eq(comparator_13_eq));  // open: gt, lt
  Comparator #(.Bits(20)) comparator_14 (.a(ZoomFactor), .b(20'h2000), .eq(comparator_14_eq));  // open: gt, lt
  Comparator #(.Bits(20)) comparator_15 (.a(ZoomFactor), .b(20'h4000), .eq(comparator_15_eq));  // open: gt, lt
  Comparator #(.Bits(20)) comparator_16 (.a(ZoomFactor), .b(20'h8000), .eq(comparator_16_eq));  // open: gt, lt
  Comparator #(.Bits(20)) comparator_17 (.a(ZoomFactor), .b(20'h10000), .eq(comparator_17_eq));  // open: gt, lt
  Comparator #(.Bits(20)) comparator_18 (.a(ZoomFactor), .b(20'h20000), .eq(comparator_18_eq));  // open: gt, lt
  Comparator #(.Bits(20)) comparator_19 (.a(ZoomFactor), .b(20'h40000), .eq(comparator_19_eq));  // open: gt, lt
  Comparator #(.Bits(20)) comparator_20 (.a(ZoomFactor), .b(20'h80000), .eq(comparator_20_eq));  // open: gt, lt
  Multiplexer #(.Bits(4)) multiplexer_1 (
    .sel(comparator_20_eq), .in_0(4'b0000), .in_1(4'b0100), .out(multiplexer_1_out));
  assign _5 = multiplexer_1_out | multiplexer_2_out | multiplexer_3_out;  // Or or_1, 4 bits wide
  Multiplexer #(.Bits(4)) multiplexer_2 (
    .sel(comparator_19_eq), .in_0(4'b0000), .in_1(4'b0010), .out(multiplexer_2_out));
  Multiplexer #(.Bits(4)) multiplexer_3 (
    .sel(comparator_18_eq), .in_0(4'b0000), .in_1(4'b0001), .out(multiplexer_3_out));
  Multiplexer #(.Bits(4)) multiplexer_4 (
    .sel(comparator_17_eq), .in_0(4'b0000), .in_1(4'b0101), .out(multiplexer_4_out));
  assign _4 = multiplexer_4_out | multiplexer_5_out | multiplexer_6_out;  // Or or_2, 4 bits wide
  Multiplexer #(.Bits(4)) multiplexer_5 (
    .sel(comparator_16_eq), .in_0(4'b0000), .in_1(4'b0010), .out(multiplexer_5_out));
  Multiplexer #(.Bits(4)) multiplexer_6 (.sel(or_3_out), .in_0(4'b0000), .in_1(4'b0001), .out(multiplexer_6_out));
  Multiplexer #(.Bits(4)) multiplexer_7 (
    .sel(comparator_20_eq), .in_0(4'b0000), .in_1(4'b1001), .out(multiplexer_7_out));
  Multiplexer #(.Bits(4)) multiplexer_8 (
    .sel(comparator_19_eq), .in_0(4'b0000), .in_1(4'b0100), .out(multiplexer_8_out));
  Multiplexer #(.Bits(4)) multiplexer_9 (
    .sel(comparator_16_eq), .in_0(4'b0000), .in_1(4'b0101), .out(multiplexer_9_out));
  or or_3 (or_3_out, comparator_15_eq, comparator_1_eq);
  Multiplexer #(.Bits(4)) multiplexer_10 (.sel(or_4_out), .in_0(4'b0000), .in_1(4'b0110), .out(multiplexer_10_out));
  or or_4 (or_4_out, comparator_14_eq, comparator_2_eq);
  assign _3 = multiplexer_7_out | multiplexer_8_out | multiplexer_9_out | multiplexer_10_out | multiplexer_11_out | multiplexer_12_out | multiplexer_13_out;  // Or or_5, 4 bits wide
  Multiplexer #(.Bits(4)) multiplexer_11 (.sel(or_6_out), .in_0(4'b0000), .in_1(4'b0011), .out(multiplexer_11_out));
  or or_6 (or_6_out, comparator_13_eq, comparator_3_eq);
  Multiplexer #(.Bits(4)) multiplexer_12 (.sel(or_7_out), .in_0(4'b0000), .in_1(4'b0010), .out(multiplexer_12_out));
  or or_7 (or_7_out, comparator_15_eq, comparator_18_eq, comparator_1_eq);
  Multiplexer #(.Bits(4)) multiplexer_13 (.sel(or_8_out), .in_0(4'b0000), .in_1(4'b0001), .out(multiplexer_13_out));
  or or_8 (or_8_out, comparator_12_eq, comparator_17_eq, comparator_4_eq);
  Multiplexer #(.Bits(4)) multiplexer_14 (.sel(or_9_out), .in_0(4'b0000), .in_1(4'b1000), .out(multiplexer_14_out));
  or or_9 (or_9_out, comparator_1_eq, comparator_5_eq, comparator_19_eq, comparator_11_eq, comparator_15_eq);
  Multiplexer #(.Bits(4)) multiplexer_15 (.sel(_1), .in_0(4'b0001), .in_1(4'b0001), .out(_0_1));
  Multiplexer #(.Bits(4)) multiplexer_16 (.sel(or_10_out), .in_0(4'b0000), .in_1(4'b0110), .out(multiplexer_16_out));
  or or_10 (or_10_out, comparator_4_eq, comparator_12_eq, comparator_16_eq, comparator_20_eq);
  assign _2 = multiplexer_14_out | multiplexer_16_out | multiplexer_17_out | multiplexer_18_out | multiplexer_19_out;  // Or or_11, 4 bits wide
  Multiplexer #(.Bits(4)) multiplexer_17 (.sel(or_12_out), .in_0(4'b0000), .in_1(4'b0100), .out(multiplexer_17_out));
  or or_12 (or_12_out, comparator_2_eq, comparator_6_eq, comparator_10_eq, comparator_14_eq, comparator_18_eq);
  Multiplexer #(.Bits(4)) multiplexer_18 (.sel(or_14_out), .in_0(4'b0000), .in_1(4'b0010), .out(multiplexer_18_out));
  or or_13 (_1, comparator_9_eq, comparator_10_eq, comparator_11_eq, comparator_12_eq, comparator_13_eq, comparator_14_eq, comparator_15_eq, comparator_16_eq, comparator_17_eq, comparator_18_eq, comparator_19_eq, comparator_20_eq);
  Multiplexer #(.Bits(4)) multiplexer_19 (
    .sel(comparator_8_eq), .in_0(4'b0000), .in_1(4'b0001), .out(multiplexer_19_out));
  or or_14 (or_14_out, comparator_3_eq, comparator_7_eq, comparator_9_eq, comparator_13_eq, comparator_17_eq);
  // Pins of 1 and 4 bits meet at _0_1
endmodule
